# Fritzing sketch Thermistor_103AT_Test (saved by Fritzing 0.9.2b)
breadboards: 1
perfboards: 1

parts:
  U1 = mystery part, 3 pins [chip_label=TL431]
  R1 = Resistor [tolerance=±5% resistance=1k package=THT]
  R3 = Resistor [tolerance=±5% resistance=10k package=THT]
  R4 = Temperature Sensor (Thermistor) [thermistor_type=NTC package=THT]
  J1 = single row smd female pin header, 9 pins [form="♀ (female)"]  # not connected
  J2 = single row smd female pin header, 9 pins [form="♀ (female)"]
  J3 = female pin header, 8 pins [form="♀ (female)"]  # not connected
  J4 = female pin header, 8 pins [form="♀ (female)"]  # not connected
  J5 = female pin header, 10 pins [form="♀ (female)"]
  J6 = female pin header, 6 pins [form="♀ (female)"]
  J7 = female pin header, 6 pins [form="♀ (female)"]

nets:
  N1: U1.pin1, U1.pin3, R1.Pin_0
  N2: U1.pin2, R3.Pin_1
  N3: R3.Pin_0, R4.pin_1
  N4: R4.pin_0, J2.pin2, J5.pin8
  N5: J5.pin9, J6.pin5
  N6: J5.pin10, J7.pin5

notes:
  TL431
  REF
  ANODE
  CATHODE
  GND
  +5V
  V_therm
  V_hi
  PSoC 4 Pioneer Kit
  ADC
  Vref
